# Fritzing sketch Vox_Imperium (saved by Fritzing 0.9.2b)
breadboards: 2

parts:
  Part1 = Power Cell LiPo Charger/Booster  # not connected
  Part2 = Breakout Board for Electret Microphone
  SP1 = SPEAKER [package=pcb_mount_speaker]  # not connected
  SP2 = SPEAKER [package=pcb_mount_speaker]  # not connected
  R2 = Resistor [tolerance=±5% resistance=2.2k package="2010 [SMD]"]
  R3 = Resistor [tolerance=±5% resistance=4.7k package="2010 [SMD]"]

nets:
  N1: Part2.VCC, R3.Pin_1
  N2: Part2.GND, R2.Pin_1
  N3: R2.Pin_0, R3.Pin_0
